// Logisim project control.circ as structural Verilog: 1 circuit, main circuit Control Unit
module Control_Unit (
  input  start,
  input  add,
  input  exit,
  input  clock,
  output last_check,
  output multi_zero,
  output load_product,
  output add_2
);

  wire and_1_out, and_2_out, and_3_out, and_6_out, and_7_out, and_8_out, and_9_out, and_10_out, and_11_out,
       not_1_out, not_2_out, not_3_out, not_4_out, not_5_out, not_6_out, not_7_out, or_1_out;
  wire [2:0] N0_out, register_1_q;

  not not_1 (not_1_out, start);
  not not_2 (not_2_out, add);
  not not_3 (not_3_out, exit);
  Register #(.width(3)) register_1 (.D(N0_out), .Q(register_1_q), .clk(clock));  // open: en, clr
  not not_4 (not_4_out, register_1_q[2]);
  not not_5 (not_5_out, register_1_q[0]);
  not not_6 (not_6_out, register_1_q[1]);
  and and_1 (and_1_out, not_4_out, not_6_out, not_5_out);
  and and_2 (and_2_out, not_4_out, register_1_q[1], register_1_q[0]);
  and and_3 (and_3_out, not_4_out, register_1_q[1], not_5_out);
  not not_7 (not_7_out, exit);
  or or_1 (or_1_out, and_1_out, and_2_out);
  or or_2 (load_product, and_3_out, and_2_out);
  and and_4 (last_check, not_7_out, or_1_out);
  or or_3 (multi_zero, and_2_out, and_3_out);
  and and_5 (add_2, register_1_q[0], register_1_q[1], not_4_out);
  and N2 (N0_out[2], exit, register_1_q[0], register_1_q[1], not_4_out);
  and and_6 (and_6_out, not_4_out, not_6_out, register_1_q[0]);
  and and_7 (and_7_out, not_4_out, register_1_q[1], not_5_out);
  and and_8 (and_8_out, not_4_out, not_6_out, not_5_out, start);
  and and_9 (and_9_out, not_4_out, not_6_out, register_1_q[0], not_2_out);
  and and_10 (and_10_out, not_4_out, register_1_q[1], not_5_out);
  and and_11 (and_11_out, not_4_out, register_1_q[1], register_1_q[0], not_3_out);
  or N1 (N0_out[1], and_6_out, and_7_out);
  or N0 (N0_out[0], and_8_out, and_9_out, and_10_out, and_11_out);
endmodule
