// Logisim project datapath.circ as structural Verilog: 2 circuits, main circuit Datapath
module Datapath (
  input  [31:0] Multiplier,
  input  [31:0] multiplicand,
  input  MultipZero,
  input  lastCheck,
  input  clock,
  input  loadProduct,
  input  Add,
  input  Add_2,
  output [31:0] productResult,
  output [31:0] MultipilerResult,
  output add_3,
  output exit
);

  wire [31:0] adder_1_out, counter_1_q, multiplexer_1_out, multiplexer_2_out, multiplicand_q,
       shifter_1_multiplier_2, shifter_1_product_2;

  Counter #(.width(32), .max('h21), .ongoal("stay")) counter_1 (
    .Q(counter_1_q), .clk(Add_2));  // open: load, D, count, carry, clr
  Multiplexer #(.width(32)) multiplexer_1 (
    .in0(Multiplier), .in1(shifter_1_multiplier_2), .out(multiplexer_1_out), .sel(MultipZero), .en(1'b1));
  Register #(.width(32)) u_Multiplier (
    .D(multiplexer_1_out), .en(lastCheck), .Q(MultipilerResult), .clk(clock));  // open: clr
  Comparator #(.width(32)) comparator_1 (.a(counter_1_q), .b(32'h21), .eq(exit));  // open: gt, lt
  Register #(.width(32)) u_multiplicand (.D(multiplicand), .en(1'b1), .Q(multiplicand_q), .clk(clock));  // open: clr
  Multiplexer #(.width(32)) multiplexer_2 (
    .in0(adder_1_out), .in1(shifter_1_product_2), .out(multiplexer_2_out), .sel(Add), .en(1'b1));
  Register #(.width(32)) product (
    .D(multiplexer_2_out), .en(loadProduct), .Q(productResult), .clk(clock));  // open: clr
  Adder #(.width(32)) adder_1 (.a(multiplicand_q), .b(productResult), .out(adder_1_out));  // open: cin, cout
  shifter shifter_1 (
    .multiplier(MultipilerResult), .product(productResult), .multiplier_2(shifter_1_multiplier_2),
    .product_2(shifter_1_product_2));
  Comparator #(.width(1)) comparator_2 (.a(MultipilerResult[0]), .b(1'b1), .eq(add_3));  // open: gt, lt
endmodule

// shifteee
module shifter (
  input  [31:0] multiplier,
  input  [31:0] product,
  output [31:0] multiplier_2,
  output [31:0] product_2
);


  assign multiplier_2 = {product[0], multiplier[31:1]};
  assign product_2 = {1'b0, product[31:1]};
endmodule
