// Logisim project mult32.circ as structural Verilog: 1 circuit, main circuit Mult32
module Mult32 (
  input  [31:0] Multiplier,
  input  [31:0] Multiplicand,
  output [31:0] out_3,
  output [31:0] out_4
);

  wire Clock_out, Control_Unit_add_2, Control_Unit_last_check, Control_Unit_load_product,
       Control_Unit_multi_zero, Datapath_add_3, Datapath_exit, Start_out;

  Clock Clock (.out(Clock_out));
  Datapath Datapath (
    .Multiplier(Multiplier), .multiplicand(Multiplicand), .productResult(out_3), .MultipilerResult(out_4),
    .MultipZero(Control_Unit_multi_zero), .lastCheck(Control_Unit_last_check), .clock(Clock_out),
    .loadProduct(Control_Unit_load_product), .Add(Control_Unit_add_2), .Add_2(Control_Unit_add_2),
    .exit(Datapath_exit), .add_3(Datapath_add_3));
  Control_Unit Control_Unit (
    .start(Start_out), .add(Datapath_add_3), .exit(Datapath_exit), .clock(Clock_out),
    .last_check(Control_Unit_last_check), .multi_zero(Control_Unit_multi_zero),
    .load_product(Control_Unit_load_product), .add_2(Control_Unit_add_2));
  Button Start (.out(Start_out));

  // Notes on the sheet:
  //   Result
endmodule
